// Logisim project Blake3000.circ as structural Verilog: 3 circuits, main circuit main
module main (
  input  [7:0] I,
  input  CLOCK
);

  wire control_unit_1_accumulator_write, control_unit_1_alu_operation, control_unit_1_program_counter_write,
       control_unit_1_ram_write;
  wire [1:0] control_unit_1_accumulator_select, control_unit_1_program_counter_select;
  wire [4:0] adder_1_out, adder_2_out, control_unit_1_address, multiplexer_1_out, PROGRAM_COUNTER_q;
  wire [7:0] ACCUMULATOR_q, alu_1_o, multiplexer_2_out, ram_1_dout, rom_1_data;

  Adder #(.width(5)) adder_1 (.a(control_unit_1_address), .b(5'b00001), .out(adder_1_out));  // open: cin, cout
  Adder #(.width(5)) adder_2 (.a(control_unit_1_address), .b(5'b00010), .out(adder_2_out));  // open: cin, cout
  Register #(.width(5)) PROGRAM_COUNTER (
    .D(multiplexer_1_out), .en(control_unit_1_program_counter_write), .clk(CLOCK), .Q(PROGRAM_COUNTER_q));  // open: clr
  Multiplexer #(.select(2), .width(5)) multiplexer_1 (
    .in0(control_unit_1_address), .in1(adder_1_out), .in2(adder_2_out), .out(multiplexer_1_out),
    .sel(control_unit_1_program_counter_select));  // open: in3
  ROM #(.addrWidth(5)) rom_1 (.addr(PROGRAM_COUNTER_q), .data(rom_1_data));
  Register ACCUMULATOR (
    .D(multiplexer_2_out), .en(control_unit_1_accumulator_write), .clk(CLOCK), .Q(ACCUMULATOR_q));  // open: clr
  Multiplexer #(.select(2), .width(8)) multiplexer_2 (
    .in0(I), .in1(ram_1_dout), .in2(alu_1_o), .out(multiplexer_2_out), .sel(control_unit_1_accumulator_select));  // open: in3
  RAM #(.addrWidth(5), .enables("line")) ram_1 (
    .addr(control_unit_1_address), .we(control_unit_1_ram_write), .clk(CLOCK), .din(ACCUMULATOR_q),
    .dout(ram_1_dout));
  CONTROL_UNIT control_unit_1 (
    .ACCUMULATOR_VALUE(ACCUMULATOR_q), .I(rom_1_data), .ALU_OPERATION(control_unit_1_alu_operation),
    .PROGRAM_COUNTER_WRITE(control_unit_1_program_counter_write),
    .PROGRAM_COUNTER_SELECT(control_unit_1_program_counter_select),
    .ACCUMULATOR_WRITE(control_unit_1_accumulator_write),
    .ACCUMULATOR_SELECT(control_unit_1_accumulator_select), .RAM_WRITE(control_unit_1_ram_write),
    .ADDRESS(control_unit_1_address));
  ALU alu_1 (.SEL(control_unit_1_alu_operation), .A(ACCUMULATOR_q), .B(ram_1_dout), .O(alu_1_o));
endmodule

module ALU (
  input  SEL,
  input  [7:0] A,
  input  [7:0] B,
  output [7:0] O
);

  wire [7:0] adder_1_out, subtractor_1_out;

  Adder adder_1 (.a(A), .b(B), .out(adder_1_out));  // open: cin, cout
  Multiplexer #(.width(8)) multiplexer_1 (.in0(adder_1_out), .in1(subtractor_1_out), .out(O), .sel(SEL));
  Subtractor subtractor_1 (.a(A), .b(B), .out(subtractor_1_out));  // open: bin, bout
endmodule

module CONTROL_UNIT (
  input  [7:0] ACCUMULATOR_VALUE,
  input  [7:0] I,
  output ALU_OPERATION,
  output PROGRAM_COUNTER_WRITE,
  output [1:0] PROGRAM_COUNTER_SELECT,
  output ACCUMULATOR_WRITE,
  output [1:0] ACCUMULATOR_SELECT,
  output RAM_WRITE,
  output [4:0] ADDRESS
);

  wire [7:0] and_1_out, and_2_out, multiplexer_1_out, multiplexer_2_out, nand_1_out;

  assign and_1_out = ACCUMULATOR_VALUE & 8'h80;  // AND_Gate and_1, 8 bits wide
  assign nand_1_out = ~(ACCUMULATOR_VALUE & {8{1'b0}});  // NAND_Gate nand_1, 8 bits wide
  assign and_2_out = ACCUMULATOR_VALUE & 8'h7f;  // AND_Gate and_2, 8 bits wide
  Multiplexer #(.select(2), .width(8)) multiplexer_1 (
    .in0(and_1_out), .in1(nand_1_out), .in2(and_2_out), .out(multiplexer_1_out), .sel(I[4:3]));  // open: in3
  Multiplexer #(.width(8)) multiplexer_2 (
    .in0(8'h50), .in1(8'h60), .out(multiplexer_2_out), .sel(multiplexer_1_out[7]));
  Multiplexer #(.select(3), .width(8)) multiplexer_3 (
    .in0(8'h58), .in1(8'h5a), .in2(8'h51), .in3(8'h5c), .in4(8'hdc), .in5(8'h40), .in6(multiplexer_2_out),
    .in7({8{1'b0}}),
    .out({ALU_OPERATION, PROGRAM_COUNTER_WRITE, PROGRAM_COUNTER_SELECT, ACCUMULATOR_WRITE, ACCUMULATOR_SELECT, RAM_WRITE}),
    .sel(I[7:5]));

  assign ADDRESS = I[4:0];
endmodule
